// Logisim project Comparison.circ as structural Verilog: 1 circuit, main circuit main
module main (
  input  in_1,
  input  in_2,
  output PGQ,
  output EG,
  output PPQ
);

  wire not_1_out, not_2_out, not_3_out;

  not not_1 (not_1_out, in_2);
  not not_2 (not_2_out, in_2);
  not not_3 (not_3_out, in_1);
  and and_1 (PGQ, in_1, not_1_out);
  xor xor_1 (EG, in_1, not_2_out);
  and and_2 (PPQ, in_2, not_3_out);
endmodule
