// Logisim project additionneur.circ as structural Verilog: 3 circuits, main circuit main
module main (
  input  in_1,
  input  in_2,
  input  in_3,
  output out_4,
  output out_5
);

  wire and_1_out, and_2_out, xor_1_out;

  xor xor_1 (xor_1_out, in_1, in_2);
  xor xor_2 (out_4, xor_1_out, in_3);
  and and_1 (and_1_out, in_3, xor_1_out);
  and and_2 (and_2_out, in_2, in_1);
  or or_1 (out_5, and_1_out, and_2_out);
endmodule

module addition (
  input  in_1,
  input  [2:0] in_2,
  input  [2:0] in_3,
  output [2:0] out_4,
  output out_5
);

  wire main_1_out_5, main_2_out_5;

  main main_1 (.in_1(in_2[0]), .in_2(in_3[0]), .in_3(in_1), .out_4(out_4[0]), .out_5(main_1_out_5));
  main main_2 (.in_1(in_2[1]), .in_2(in_3[1]), .in_3(main_1_out_5), .out_4(out_4[1]), .out_5(main_2_out_5));
  main main_3 (.in_1(in_2[2]), .in_2(in_3[2]), .in_3(main_2_out_5), .out_4(out_4[2]), .out_5(out_5));
endmodule

module demi_soustracteur (
  input  in_1,
  input  in_2
);
endmodule
