// Logisim project digital_display.circ as structural Verilog: 3 circuits, main circuit main
module main (
  input  [2:0] in_1,
  input  [2:0] in_2
);

  wire v2_1_a, v2_1_b, v2_1_c, v2_1_d, v2_1_e, v2_1_f, v2_1_g, v2_2_a, v2_2_c, v2_2_d, v2_2_e, v2_2_f, v2_2_g;

  v2 v2_1 (
    .e1(in_1[1]), .e2(in_1[1]), .e3(in_1[2]), .a(v2_1_a), .b(v2_1_b), .c(v2_1_c), .d(v2_1_d), .e(v2_1_e),
    .f(v2_1_f), .g(v2_1_g));
  v2 v2_2 (
    .e1(in_2[1]), .e2(in_2[1]), .e3(in_2[2]), .a(v2_2_a), .b(v2_2_a), .c(v2_2_c), .d(v2_2_d), .e(v2_2_e),
    .f(v2_2_f), .g(v2_2_g));
  _7_Segment_Display u_7_segment_display_1 (
    .g(v2_1_g), .f(v2_1_f), .a(v2_1_a), .b(v2_1_b), .e(v2_1_e), .d(v2_1_d), .c(v2_1_c));  // open: dp
  _7_Segment_Display u_7_segment_display_2 (
    .g(v2_2_g), .f(v2_2_f), .a(v2_2_a), .b(v2_2_a), .e(v2_2_e), .d(v2_2_d), .c(v2_2_c));  // open: dp

  assign in_1[0] = in_1[1];
  assign in_2[0] = in_2[1];
endmodule

module digital_display (
  input  e1,
  input  e2,
  input  e3,
  output a,
  output b,
  output c,
  output d,
  output e,
  output f,
  output g
);

  wire and_1_out, and_2_out, not_1_out, not_2_out, not_3_out, not_4_out, not_5_out, not_6_out, not_7_out,
       not_8_out, not_9_out;

  not not_1 (not_1_out, e1);
  not not_2 (not_2_out, e2);
  not not_3 (not_3_out, e2);
  not not_4 (not_4_out, e3);
  not not_5 (not_5_out, e3);
  not not_6 (not_6_out, e1);
  not not_7 (not_7_out, e2);
  not not_8 (not_8_out, e3);
  not not_9 (not_9_out, e3);
  or or_1 (g, e3, e1);
  or or_2 (a, not_1_out, not_2_out, e3);
  or or_3 (b, not_3_out, not_4_out, e1);
  or or_4 (c, not_5_out, e2, e1);
  and and_1 (and_1_out, not_6_out, not_7_out);
  and and_2 (and_2_out, e2, not_8_out);
  or or_5 (f, not_9_out, e2, e1);
  or or_6 (e, and_1_out, and_2_out);

  assign d = 1'b1;
endmodule

module v2 (
  input  e1,
  input  e2,
  input  e3,
  output a,
  output b,
  output c,
  output d,
  output e,
  output f,
  output g
);

  wire and_1_out, and_2_out, and_3_out, and_4_out, and_5_out, and_6_out, and_7_out, and_8_out, and_9_out,
       and_10_out, and_11_out, and_12_out, and_13_out, and_14_out, and_15_out, and_16_out, not_1_out,
       not_2_out, not_3_out, not_4_out, not_5_out, not_6_out, not_7_out, not_8_out, not_9_out, not_10_out,
       not_11_out, not_12_out, not_13_out, not_14_out, not_15_out, not_16_out, not_17_out, not_18_out,
       not_19_out, not_20_out, not_21_out;

  not not_1 (not_1_out, e1);
  not not_2 (not_2_out, e3);
  not not_3 (not_3_out, e2);
  not not_4 (not_4_out, e3);
  not not_5 (not_5_out, e2);
  not not_6 (not_6_out, e1);
  not not_7 (not_7_out, e3);
  not not_8 (not_8_out, e1);
  not not_9 (not_9_out, e3);
  not not_10 (not_10_out, e2);
  not not_11 (not_11_out, e1);
  not not_12 (not_12_out, e3);
  not not_13 (not_13_out, e3);
  not not_14 (not_14_out, e2);
  not not_15 (not_15_out, e3);
  not not_16 (not_16_out, e2);
  not not_17 (not_17_out, e3);
  not not_18 (not_18_out, e1);
  not not_19 (not_19_out, e2);
  not not_20 (not_20_out, e3);
  and and_1 (and_1_out, not_1_out, not_2_out);
  and and_2 (and_2_out, e1, e3);
  not not_21 (not_21_out, e1);
  and and_3 (and_3_out, not_3_out, not_4_out);
  and and_4 (and_4_out, e2, e3);
  or or_1 (c, not_5_out, e3, e1);
  and and_5 (and_5_out, not_6_out, not_7_out);
  and and_6 (and_6_out, not_8_out, e2);
  and and_7 (and_7_out, e2, not_9_out);
  and and_8 (and_8_out, e1, not_10_out, e3);
  and and_9 (and_9_out, not_11_out, not_12_out);
  and and_10 (and_10_out, e2, not_13_out);
  and and_11 (and_11_out, not_14_out, not_15_out);
  and and_12 (and_12_out, e1, not_16_out);
  and and_13 (and_13_out, e1, not_17_out);
  and and_14 (and_14_out, not_18_out, e2);
  and and_15 (and_15_out, e1, not_19_out);
  and and_16 (and_16_out, e1, not_20_out);
  or or_2 (a, and_1_out, e2, and_2_out);
  or or_3 (b, not_21_out, and_3_out, and_4_out);
  or or_4 (d, and_5_out, and_6_out, and_7_out, and_8_out);
  or or_5 (e, and_9_out, and_10_out);
  or or_6 (f, and_11_out, and_12_out, and_13_out);
  or or_7 (g, and_14_out, and_15_out, and_16_out);
endmodule
